# Fritzing sketch DoolhofOntwerp (saved by Fritzing 0.9.2b)
breadboards: 3

parts:
  U1 = 74HC595 [package="DIP16 [THT]"]
  U2 = 74HC595 [package="DIP16 [THT]"]
  Part1 = LED Matrix - Serial Interface - Red/Green/Blue
  R1 = Resistor [tolerance=±5% resistance=220 package=THT]
  R2 = Resistor [tolerance=±5% resistance=220 package=THT]
  R3 = Resistor [tolerance=±5% resistance=220 package=THT]
  R4 = Resistor [tolerance=±5% resistance=220 package=THT]
  R5 = Resistor [tolerance=±5% resistance=220 package=THT]
  R6 = Resistor [tolerance=±5% resistance=220 package=THT]
  R7 = Resistor [tolerance=±5% resistance=220 package=THT]
  R8 = Resistor [tolerance=±5% resistance=220 package=THT]
  Part2 = Arduino Uno (Rev3)
  S1 = Pushbutton [package="[THT]"]
  S2 = Pushbutton [package="[THT]"]
  S3 = Pushbutton [package="[THT]"]
  S4 = Pushbutton [package="[THT]"]
  R9 = Resistor [tolerance=±5% resistance=220 package=THT]
  R10 = Resistor [tolerance=±5% resistance=220 package=THT]
  R11 = Resistor [tolerance=±5% resistance=220 package=THT]
  R12 = Resistor [tolerance=±5% resistance=220 package=THT]
  J1 = Piezo Speaker

nets:
  N1: U1.Q1, R2.Pin_1
  N2: U1.Q2, R3.Pin_1
  N3: U1.Q3, R4.Pin_1
  N4: U1.Q4, R5.Pin_1
  N5: U1.Q5, R6.Pin_1
  N6: U1.Q6, R7.Pin_1
  N7: U1.Q7, R8.Pin_1
  GND: U1.GND, U1.OE, U2.GND, Part2.GND, R9.Pin_1, R10.Pin_1, R11.Pin_1, R12.Pin_1, J1.pin1
  N8: U1.Q7', U2.DS
  VCC: U1.MR, U1.VCC, U2.MR, U2.VCC, Part2.3V3
  N9: U1.SH_CP, U2.SH_CP, Part2.D12/MISO
  N10: U1.ST_CP, U2.ST_CP, Part2.D8
  N11: U1.DS, Part2.D11_PWM/MOSI
  N12: U1.Q0, R1.Pin_1
  N13: U2.Q4, Part1.GND
  N14: U2.Q6, Part1.MOSI
  N15: U2.Q7, Part1.VCC, R5.Pin_0
  N16: Part1.CS, R2.Pin_0
  N17: Part1.SCK, R3.Pin_0
  N18: Part2.D2, S1.Pin_3, S1.Pin_4, R9.Pin_0
  N19: Part2.D3_PWM, S2.Pin_3, S2.Pin_4, R10.Pin_0
  N20: Part2.D4, S3.Pin_3, S3.Pin_4, R11.Pin_0
  N21: Part2.D5_PWM, S4.Pin_3, S4.Pin_4, R12.Pin_0
  N22: Part2.D7, J1.pin2
  N23: Part2.5V, S1.Pin_1, S1.Pin_2, S2.Pin_1, S2.Pin_2, S3.Pin_1, S3.Pin_2, S4.Pin_1, S4.Pin_2
